// Logisim project 32bitCPU.circ as structural Verilog
module MUX2 (
  input  A,
  input  B,
  input  S,
  output X
);

  wire and_1_out, and_2_out, not_1_out;

  not not_1 (not_1_out, S);
  and and_1 (and_1_out, A, not_1_out);
  and and_2 (and_2_out, S, B);
  or or_1 (X, and_1_out, and_2_out);
endmodule

module Adder (
  input  CarryIn,
  input  A,
  input  B,
  output CarryOut,
  output Sum
);

  wire and_1_out, and_2_out, and_3_out, and_4_out, xor_1_out;

  and and_1 (and_1_out, CarryIn, B);
  ExactlyOne xor_1 (.out(xor_1_out), .in0(CarryIn), .in1(A), .in2(B));
  and and_2 (and_2_out, CarryIn, B, A);
  and and_3 (and_3_out, CarryIn, A);
  or or_1 (CarryOut, and_3_out, and_1_out, and_4_out);
  and and_4 (and_4_out, A, B);
  or or_2 (Sum, xor_1_out, and_2_out);
endmodule

module ALU1 (
  input  Ainvert,
  input  CarryIn,
  input  A,
  input  O2,
  input  O1,
  input  Binvert,
  input  B,
  input  Less,
  output Result,
  output CarryOut
);

  wire adder_1_sum, and_1_out, mux2_1_x, mux2_2_x, not_1_out, not_2_out, or_1_out;

  not not_1 (not_1_out, A);
  not not_2 (not_2_out, B);
  MUX2 mux2_1 (.A(A), .B(not_1_out), .S(Ainvert), .X(mux2_1_x));
  MUX2 mux2_2 (.A(B), .B(not_2_out), .S(Binvert), .X(mux2_2_x));
  Adder adder_1 (.A(mux2_1_x), .B(mux2_2_x), .CarryIn(CarryIn), .Sum(adder_1_sum), .CarryOut(CarryOut));
  and and_1 (and_1_out, mux2_1_x, mux2_2_x);
  or or_1 (or_1_out, mux2_1_x, mux2_2_x);
  MUX4 mux4_1 (.A(and_1_out), .B(or_1_out), .C(adder_1_sum), .D(Less), .S1(O1), .S2(O2), .X(Result));
endmodule

module MUX4 (
  input  A,
  input  B,
  input  C,
  input  D,
  input  S1,
  input  S2,
  output X
);

  wire and_1_out, and_2_out, and_3_out, and_4_out, not_1_out, not_2_out, not_3_out, not_4_out;

  not not_1 (not_1_out, S1);
  not not_2 (not_2_out, S2);
  not not_3 (not_3_out, S1);
  not not_4 (not_4_out, S2);
  and and_1 (and_1_out, A, not_1_out, not_2_out);
  and and_2 (and_2_out, B, not_3_out, S2);
  and and_3 (and_3_out, C, S1, not_4_out);
  and and_4 (and_4_out, D, S1, S2);
  or or_1 (X, and_1_out, and_2_out, and_3_out, and_4_out);
endmodule

module ALU32 (
  input  [3:0] Operation,
  input  [31:0] A,
  input  Overflow,
  input  [31:0] B,
  output Zero,
  output [31:0] Result
);

  wire alu1_1_carryout, alu1_1_result, alu1_2_carryout, alu1_2_result, alu1_3_carryout, alu1_3_result,
       alu1_4_carryout, alu1_4_result, alu1_5_carryout, alu1_5_result, alu1_6_carryout, alu1_6_result,
       alu1_7_carryout, alu1_7_result, alu1_8_carryout, alu1_8_result, alu1_9_carryout, alu1_9_result,
       alu1_10_carryout, alu1_10_result, alu1_11_carryout, alu1_11_result, alu1_12_carryout, alu1_12_result,
       alu1_13_carryout, alu1_13_result, alu1_14_carryout, alu1_14_result, alu1_15_carryout, alu1_15_result,
       alu1_16_carryout, alu1_16_result, alu1_17_carryout, alu1_17_result, alu1_18_carryout, alu1_18_result,
       alu1_19_carryout, alu1_19_result, alu1_20_carryout, alu1_20_result, alu1_21_carryout, alu1_21_result,
       alu1_22_carryout, alu1_22_result, alu1_23_carryout, alu1_23_result, alu1_24_carryout, alu1_24_result,
       alu1_25_carryout, alu1_25_result, alu1_26_carryout, alu1_26_result, alu1_27_carryout, alu1_27_result,
       alu1_28_carryout, alu1_28_result, alu1_29_carryout, alu1_29_result, alu1_30_carryout, alu1_30_result,
       alu1_31_carryout, alu1_31_result, alu1_32_result, bitconv1_1_b0, bitconv1_1_b1, bitconv1_1_b2,
       bitconv1_1_b3, bitconv1_1_b4, bitconv1_1_b5, bitconv1_1_b6, bitconv1_1_b7, bitconv1_1_b8,
       bitconv1_1_b9, bitconv1_1_b10, bitconv1_1_b11, bitconv1_1_b12, bitconv1_1_b13, bitconv1_1_b14,
       bitconv1_1_b15, bitconv1_1_b16, bitconv1_1_b17, bitconv1_1_b18, bitconv1_1_b19, bitconv1_1_b20,
       bitconv1_1_b21, bitconv1_1_b22, bitconv1_1_b23, bitconv1_1_b24, bitconv1_1_b25, bitconv1_1_b26,
       bitconv1_1_b27, bitconv1_1_b28, bitconv1_1_b29, bitconv1_1_b30, bitconv1_1_b31, bitconv1_2_b0,
       bitconv1_2_b1, bitconv1_2_b2, bitconv1_2_b3, bitconv1_2_b4, bitconv1_2_b5, bitconv1_2_b6,
       bitconv1_2_b7, bitconv1_2_b8, bitconv1_2_b9, bitconv1_2_b10, bitconv1_2_b11, bitconv1_2_b12,
       bitconv1_2_b13, bitconv1_2_b14, bitconv1_2_b15, bitconv1_2_b16, bitconv1_2_b17, bitconv1_2_b18,
       bitconv1_2_b19, bitconv1_2_b20, bitconv1_2_b21, bitconv1_2_b22, bitconv1_2_b23, bitconv1_2_b24,
       bitconv1_2_b25, bitconv1_2_b26, bitconv1_2_b27, bitconv1_2_b28, bitconv1_2_b29, bitconv1_2_b30,
       bitconv1_2_b31, or_1_out, undriven, undriven_2, undriven_3, undriven_4;

  BitConv1 bitconv1_1 (
    .Bit32(A), .B2(bitconv1_1_b2), .B3(bitconv1_1_b3), .B4(bitconv1_1_b4), .B5(bitconv1_1_b5),
    .B6(bitconv1_1_b6), .B7(bitconv1_1_b7), .B8(bitconv1_1_b8), .B9(bitconv1_1_b9), .B10(bitconv1_1_b10),
    .B11(bitconv1_1_b11), .B12(bitconv1_1_b12), .B13(bitconv1_1_b13), .B14(bitconv1_1_b14),
    .B0(bitconv1_1_b0), .B15(bitconv1_1_b15), .B16(bitconv1_1_b16), .B17(bitconv1_1_b17),
    .B18(bitconv1_1_b18), .B19(bitconv1_1_b19), .B20(bitconv1_1_b20), .B21(bitconv1_1_b21),
    .B22(bitconv1_1_b22), .B23(bitconv1_1_b23), .B24(bitconv1_1_b24), .B1(bitconv1_1_b1),
    .B25(bitconv1_1_b25), .B26(bitconv1_1_b26), .B27(bitconv1_1_b27), .B28(bitconv1_1_b28),
    .B29(bitconv1_1_b29), .B30(bitconv1_1_b30), .B31(bitconv1_1_b31));
  BitConv1 bitconv1_2 (
    .Bit32(B), .B2(bitconv1_2_b2), .B3(bitconv1_2_b3), .B4(bitconv1_2_b4), .B5(bitconv1_2_b5),
    .B6(bitconv1_2_b6), .B7(bitconv1_2_b7), .B8(bitconv1_2_b8), .B9(bitconv1_2_b9), .B10(bitconv1_2_b10),
    .B11(bitconv1_2_b11), .B12(bitconv1_2_b12), .B13(bitconv1_2_b13), .B14(bitconv1_2_b14),
    .B0(bitconv1_2_b0), .B15(bitconv1_2_b15), .B16(bitconv1_2_b16), .B17(bitconv1_2_b17),
    .B18(bitconv1_2_b18), .B19(bitconv1_2_b19), .B20(bitconv1_2_b20), .B21(bitconv1_2_b21),
    .B22(bitconv1_2_b22), .B23(bitconv1_2_b23), .B24(bitconv1_2_b24), .B1(bitconv1_2_b1),
    .B25(bitconv1_2_b25), .B26(bitconv1_2_b26), .B27(bitconv1_2_b27), .B28(bitconv1_2_b28),
    .B29(bitconv1_2_b29), .B30(bitconv1_2_b30), .B31(bitconv1_2_b31));
  ALUopConv aluopconv_1 (.ALUop(Operation), .Ainvert(undriven), .Binvert(undriven_2), .O1(undriven_3), .O2(undriven_4));
  ALU1 alu1_1 (
    .A(bitconv1_1_b0), .B(bitconv1_2_b0), .Ainvert(undriven), .Binvert(undriven_2), .Less(Overflow),
    .O1(undriven_3), .O2(undriven_4), .CarryOut(alu1_1_carryout), .Result(alu1_1_result));  // open: CarryIn
  ALU1 alu1_2 (
    .A(bitconv1_1_b1), .B(bitconv1_2_b1), .Ainvert(undriven), .Binvert(undriven_2),
    .CarryIn(alu1_1_carryout), .O1(undriven_3), .O2(undriven_4), .CarryOut(alu1_2_carryout),
    .Result(alu1_2_result));  // open: Less
  ALU1 alu1_3 (
    .A(bitconv1_1_b2), .B(bitconv1_2_b2), .Ainvert(undriven), .Binvert(undriven_2),
    .CarryIn(alu1_2_carryout), .O1(undriven_3), .O2(undriven_4), .CarryOut(alu1_3_carryout),
    .Result(alu1_3_result));  // open: Less
  ALU1 alu1_4 (
    .A(bitconv1_1_b3), .B(bitconv1_2_b3), .Ainvert(undriven), .Binvert(undriven_2),
    .CarryIn(alu1_3_carryout), .O1(undriven_3), .O2(undriven_4), .CarryOut(alu1_4_carryout),
    .Result(alu1_4_result));  // open: Less
  ALU1 alu1_5 (
    .A(bitconv1_1_b4), .B(bitconv1_2_b4), .Ainvert(undriven), .Binvert(undriven_2),
    .CarryIn(alu1_4_carryout), .O1(undriven_3), .O2(undriven_4), .CarryOut(alu1_5_carryout),
    .Result(alu1_5_result));  // open: Less
  ALU1 alu1_6 (
    .A(bitconv1_1_b5), .B(bitconv1_2_b5), .Ainvert(undriven), .Binvert(undriven_2),
    .CarryIn(alu1_5_carryout), .O1(undriven_3), .O2(undriven_4), .CarryOut(alu1_6_carryout),
    .Result(alu1_6_result));  // open: Less
  ALU1 alu1_7 (
    .A(bitconv1_1_b6), .B(bitconv1_2_b6), .Ainvert(undriven), .Binvert(undriven_2),
    .CarryIn(alu1_6_carryout), .O1(undriven_3), .O2(undriven_4), .CarryOut(alu1_7_carryout),
    .Result(alu1_7_result));  // open: Less
  ALU1 alu1_8 (
    .A(bitconv1_1_b7), .B(bitconv1_2_b7), .Ainvert(undriven), .Binvert(undriven_2),
    .CarryIn(alu1_7_carryout), .O1(undriven_3), .O2(undriven_4), .CarryOut(alu1_8_carryout),
    .Result(alu1_8_result));  // open: Less
  ALU1 alu1_9 (
    .A(bitconv1_1_b8), .B(bitconv1_2_b8), .Ainvert(undriven), .Binvert(undriven_2),
    .CarryIn(alu1_8_carryout), .O1(undriven_3), .O2(undriven_4), .CarryOut(alu1_9_carryout),
    .Result(alu1_9_result));  // open: Less
  ALU1 alu1_10 (
    .A(bitconv1_1_b9), .B(bitconv1_2_b9), .Ainvert(undriven), .Binvert(undriven_2),
    .CarryIn(alu1_9_carryout), .O1(undriven_3), .O2(undriven_4), .CarryOut(alu1_10_carryout),
    .Result(alu1_10_result));  // open: Less
  ALU1 alu1_11 (
    .A(bitconv1_1_b10), .B(bitconv1_2_b10), .Ainvert(undriven), .Binvert(undriven_2),
    .CarryIn(alu1_10_carryout), .O1(undriven_3), .O2(undriven_4), .CarryOut(alu1_11_carryout),
    .Result(alu1_11_result));  // open: Less
  ALU1 alu1_12 (
    .A(bitconv1_1_b11), .B(bitconv1_2_b11), .Ainvert(undriven), .Binvert(undriven_2),
    .CarryIn(alu1_11_carryout), .O1(undriven_3), .O2(undriven_4), .CarryOut(alu1_12_carryout),
    .Result(alu1_12_result));  // open: Less
  ALU1 alu1_13 (
    .A(bitconv1_1_b12), .B(bitconv1_2_b12), .Ainvert(undriven), .Binvert(undriven_2),
    .CarryIn(alu1_12_carryout), .O1(undriven_3), .O2(undriven_4), .CarryOut(alu1_13_carryout),
    .Result(alu1_13_result));  // open: Less
  ALU1 alu1_14 (
    .A(bitconv1_1_b13), .B(bitconv1_2_b13), .Ainvert(undriven), .Binvert(undriven_2),
    .CarryIn(alu1_13_carryout), .O1(undriven_3), .O2(undriven_4), .CarryOut(alu1_14_carryout),
    .Result(alu1_14_result));  // open: Less
  ALU1 alu1_15 (
    .A(bitconv1_1_b14), .B(bitconv1_2_b14), .Ainvert(undriven), .Binvert(undriven_2),
    .CarryIn(alu1_14_carryout), .O1(undriven_3), .O2(undriven_4), .CarryOut(alu1_15_carryout),
    .Result(alu1_15_result));  // open: Less
  ALU1 alu1_16 (
    .A(bitconv1_1_b15), .B(bitconv1_2_b15), .Ainvert(undriven), .Binvert(undriven_2),
    .CarryIn(alu1_15_carryout), .O1(undriven_3), .O2(undriven_4), .CarryOut(alu1_16_carryout),
    .Result(alu1_16_result));  // open: Less
  ALU1 alu1_17 (
    .A(bitconv1_1_b16), .B(bitconv1_2_b16), .Ainvert(undriven), .Binvert(undriven_2),
    .CarryIn(alu1_16_carryout), .O1(undriven_3), .O2(undriven_4), .CarryOut(alu1_17_carryout),
    .Result(alu1_17_result));  // open: Less
  ALU1 alu1_18 (
    .A(bitconv1_1_b17), .B(bitconv1_2_b17), .Ainvert(undriven), .Binvert(undriven_2),
    .CarryIn(alu1_17_carryout), .O1(undriven_3), .O2(undriven_4), .CarryOut(alu1_18_carryout),
    .Result(alu1_18_result));  // open: Less
  ALU1 alu1_19 (
    .A(bitconv1_1_b18), .B(bitconv1_2_b18), .Ainvert(undriven), .Binvert(undriven_2),
    .CarryIn(alu1_18_carryout), .O1(undriven_3), .O2(undriven_4), .CarryOut(alu1_19_carryout),
    .Result(alu1_19_result));  // open: Less
  ALU1 alu1_20 (
    .A(bitconv1_1_b19), .B(bitconv1_2_b19), .Ainvert(undriven), .Binvert(undriven_2),
    .CarryIn(alu1_19_carryout), .O1(undriven_3), .O2(undriven_4), .CarryOut(alu1_20_carryout),
    .Result(alu1_20_result));  // open: Less
  ALU1 alu1_21 (
    .A(bitconv1_1_b20), .B(bitconv1_2_b20), .Ainvert(undriven), .Binvert(undriven_2),
    .CarryIn(alu1_20_carryout), .O1(undriven_3), .O2(undriven_4), .CarryOut(alu1_21_carryout),
    .Result(alu1_21_result));  // open: Less
  ALU1 alu1_22 (
    .A(bitconv1_1_b21), .B(bitconv1_2_b21), .Ainvert(undriven), .Binvert(undriven_2),
    .CarryIn(alu1_21_carryout), .O1(undriven_3), .O2(undriven_4), .CarryOut(alu1_22_carryout),
    .Result(alu1_22_result));  // open: Less
  ALU1 alu1_23 (
    .A(bitconv1_1_b22), .B(bitconv1_2_b22), .Ainvert(undriven), .Binvert(undriven_2),
    .CarryIn(alu1_22_carryout), .O1(undriven_3), .O2(undriven_4), .CarryOut(alu1_23_carryout),
    .Result(alu1_23_result));  // open: Less
  ALU1 alu1_24 (
    .A(bitconv1_1_b23), .B(bitconv1_2_b23), .Ainvert(undriven), .Binvert(undriven_2),
    .CarryIn(alu1_23_carryout), .O1(undriven_3), .O2(undriven_4), .CarryOut(alu1_24_carryout),
    .Result(alu1_24_result));  // open: Less
  ALU1 alu1_25 (
    .A(bitconv1_1_b24), .B(bitconv1_2_b24), .Ainvert(undriven), .Binvert(undriven_2),
    .CarryIn(alu1_24_carryout), .O1(undriven_3), .O2(undriven_4), .CarryOut(alu1_25_carryout),
    .Result(alu1_25_result));  // open: Less
  ALU1 alu1_26 (
    .A(bitconv1_1_b25), .B(bitconv1_2_b25), .Ainvert(undriven), .Binvert(undriven_2),
    .CarryIn(alu1_25_carryout), .O1(undriven_3), .O2(undriven_4), .CarryOut(alu1_26_carryout),
    .Result(alu1_26_result));  // open: Less
  ALU1 alu1_27 (
    .A(bitconv1_1_b26), .B(bitconv1_2_b26), .Ainvert(undriven), .Binvert(undriven_2),
    .CarryIn(alu1_26_carryout), .O1(undriven_3), .O2(undriven_4), .CarryOut(alu1_27_carryout),
    .Result(alu1_27_result));  // open: Less
  ALU1 alu1_28 (
    .A(bitconv1_1_b27), .B(bitconv1_2_b27), .Ainvert(undriven), .Binvert(undriven_2),
    .CarryIn(alu1_27_carryout), .O1(undriven_3), .O2(undriven_4), .CarryOut(alu1_28_carryout),
    .Result(alu1_28_result));  // open: Less
  ALU1 alu1_29 (
    .A(bitconv1_1_b28), .B(bitconv1_2_b28), .Ainvert(undriven), .Binvert(undriven_2),
    .CarryIn(alu1_28_carryout), .O1(undriven_3), .O2(undriven_4), .CarryOut(alu1_29_carryout),
    .Result(alu1_29_result));  // open: Less
  ALU1 alu1_30 (
    .A(bitconv1_1_b29), .B(bitconv1_2_b29), .Ainvert(undriven), .Binvert(undriven_2),
    .CarryIn(alu1_29_carryout), .O1(undriven_3), .O2(undriven_4), .CarryOut(alu1_30_carryout),
    .Result(alu1_30_result));  // open: Less
  ALU1 alu1_31 (
    .A(bitconv1_1_b30), .B(bitconv1_2_b30), .Ainvert(undriven), .Binvert(undriven_2),
    .CarryIn(alu1_30_carryout), .O1(undriven_3), .O2(undriven_4), .CarryOut(alu1_31_carryout),
    .Result(alu1_31_result));  // open: Less
  ALU1 alu1_32 (
    .A(bitconv1_1_b31), .B(bitconv1_2_b31), .Ainvert(undriven), .Binvert(undriven_2),
    .CarryIn(alu1_31_carryout), .O1(undriven_3), .O2(undriven_4), .CarryOut(Overflow), .Result(alu1_32_result));  // open: Less
  or or_1 (or_1_out, alu1_1_result, alu1_2_result, alu1_3_result, alu1_4_result, alu1_5_result, alu1_6_result, alu1_7_result, alu1_8_result, alu1_9_result, alu1_10_result, alu1_11_result, alu1_12_result, alu1_13_result, alu1_14_result, alu1_15_result, alu1_16_result, alu1_17_result, alu1_18_result, alu1_19_result, alu1_20_result, alu1_21_result, alu1_22_result, alu1_23_result, alu1_24_result, alu1_25_result, alu1_26_result, alu1_27_result, alu1_28_result, alu1_29_result, alu1_30_result, alu1_31_result, alu1_32_result);
  not not_1 (Zero, or_1_out);
  BitConv32 bitconv32_1 (
    .B2(alu1_3_result), .B3(alu1_4_result), .B4(alu1_5_result), .B5(alu1_6_result), .B6(alu1_7_result),
    .B7(alu1_8_result), .B8(alu1_9_result), .B9(alu1_10_result), .B10(alu1_11_result), .B11(alu1_12_result),
    .B12(alu1_13_result), .B13(alu1_14_result), .B14(alu1_15_result), .B0(alu1_1_result),
    .B15(alu1_16_result), .B16(alu1_17_result), .B17(alu1_18_result), .B18(alu1_19_result),
    .B19(alu1_20_result), .B20(alu1_21_result), .B21(alu1_22_result), .B22(alu1_23_result),
    .B23(alu1_24_result), .B24(alu1_25_result), .B1(alu1_2_result), .B25(alu1_26_result),
    .B26(alu1_27_result), .B27(alu1_28_result), .B28(alu1_29_result), .B29(alu1_30_result),
    .B30(alu1_31_result), .B31(alu1_32_result), .Bit32(Result));
endmodule

module BitConv32 (
  input  B0,
  input  B1,
  input  B2,
  input  B3,
  input  B4,
  input  B5,
  input  B6,
  input  B7,
  input  B8,
  input  B9,
  input  B10,
  input  B11,
  input  B12,
  input  B13,
  input  B14,
  input  B15,
  input  B16,
  input  B17,
  input  B18,
  input  B19,
  input  B20,
  input  B21,
  input  B22,
  input  B23,
  input  B24,
  input  B25,
  input  B26,
  input  B27,
  input  B28,
  input  B29,
  input  B30,
  input  B31,
  output [31:0] Bit32
);


  assign Bit32 = {B31, B30, B29, B28, B27, B26, B25, B24, B23, B22, B21, B20, B19, B18, B17, B16, B15, B14, B13, B12, B11, B10, B9, B8, B7, B6, B5, B4, B3, B2, B1, B0};
endmodule

module BitConv1 (
  input  [31:0] Bit32,
  output B0,
  output B1,
  output B2,
  output B3,
  output B4,
  output B5,
  output B6,
  output B7,
  output B8,
  output B9,
  output B10,
  output B11,
  output B12,
  output B13,
  output B14,
  output B15,
  output B16,
  output B17,
  output B18,
  output B19,
  output B20,
  output B21,
  output B22,
  output B23,
  output B24,
  output B25,
  output B26,
  output B27,
  output B28,
  output B29,
  output B30,
  output B31
);


  assign B0 = Bit32[0];
  assign B1 = Bit32[1];
  assign B2 = Bit32[2];
  assign B3 = Bit32[3];
  assign B4 = Bit32[4];
  assign B5 = Bit32[5];
  assign B6 = Bit32[6];
  assign B7 = Bit32[7];
  assign B8 = Bit32[8];
  assign B9 = Bit32[9];
  assign B10 = Bit32[10];
  assign B11 = Bit32[11];
  assign B12 = Bit32[12];
  assign B13 = Bit32[13];
  assign B14 = Bit32[14];
  assign B15 = Bit32[15];
  assign B16 = Bit32[16];
  assign B17 = Bit32[17];
  assign B18 = Bit32[18];
  assign B19 = Bit32[19];
  assign B20 = Bit32[20];
  assign B21 = Bit32[21];
  assign B22 = Bit32[22];
  assign B23 = Bit32[23];
  assign B24 = Bit32[24];
  assign B25 = Bit32[25];
  assign B26 = Bit32[26];
  assign B27 = Bit32[27];
  assign B28 = Bit32[28];
  assign B29 = Bit32[29];
  assign B30 = Bit32[30];
  assign B31 = Bit32[31];
endmodule

module DLatch (
  input  C,
  input  D,
  output Q
);

  wire and_1_out, and_2_out, nor_2_out, not_1_out;

  not not_1 (not_1_out, D);
  and and_1 (and_1_out, C, not_1_out);
  nor nor_1 (Q, and_1_out, nor_2_out);
  nor nor_2 (nor_2_out, Q, and_2_out);
  and and_2 (and_2_out, C, D);
endmodule

module ALUopConv (
  input  [3:0] ALUop,
  input  Ainvert,
  input  O2,
  input  Binvert,
  input  O1
);


  assign ALUop[3] = Ainvert;
  assign Binvert = ALUop[2];
  assign O1 = ALUop[1];
  assign O2 = ALUop[0];
endmodule

module Control (
  input  [5:0] OpCode,
  output RegDst,
  output ALUSrc,
  output MemToReg,
  output RegWrite,
  output MemRead,
  output MemWrite,
  output Branch,
  output Op1,
  output Op0
);

  wire and_1_out, and_2_out, and_3_out, and_4_out, and_5_out, and_6_out, and_7_out, and_8_out, and_9_out,
       and_10_out, and_11_out, and_12_out, and_13_out, and_14_out, and_15_out, and_16_out, not_1_out,
       not_2_out, not_3_out, not_4_out, not_5_out, not_6_out, not_7_out, not_8_out, not_9_out, not_10_out,
       not_11_out, not_12_out, not_13_out, not_14_out, not_15_out, not_16_out;

  not not_1 (not_1_out, OpCode[0]);
  not not_2 (not_2_out, OpCode[1]);
  not not_3 (not_3_out, OpCode[2]);
  not not_4 (not_4_out, OpCode[3]);
  not not_5 (not_5_out, OpCode[4]);
  not not_6 (not_6_out, OpCode[5]);
  not not_7 (not_7_out, OpCode[2]);
  not not_8 (not_8_out, OpCode[3]);
  not not_9 (not_9_out, OpCode[4]);
  not not_10 (not_10_out, OpCode[2]);
  not not_11 (not_11_out, OpCode[4]);
  not not_12 (not_12_out, OpCode[0]);
  not not_13 (not_13_out, OpCode[1]);
  not not_14 (not_14_out, OpCode[3]);
  not not_15 (not_15_out, OpCode[4]);
  not not_16 (not_16_out, OpCode[5]);
  and and_1 (and_1_out, not_1_out, not_2_out);
  and and_2 (and_2_out, not_3_out, not_4_out);
  and and_3 (and_3_out, not_5_out, not_6_out);
  and and_4 (and_4_out, OpCode[0], OpCode[1]);
  and and_5 (and_5_out, not_7_out, not_8_out);
  and and_6 (and_6_out, not_9_out, OpCode[5]);
  and and_7 (and_7_out, OpCode[0], OpCode[1]);
  and and_8 (and_8_out, not_10_out, OpCode[3]);
  and and_9 (and_9_out, not_11_out, OpCode[5]);
  and and_10 (and_10_out, not_12_out, not_13_out);
  and and_11 (and_11_out, OpCode[2], not_14_out);
  and and_12 (and_12_out, not_15_out, not_16_out);
  and and_13 (and_13_out, and_1_out, and_2_out);
  and and_14 (and_14_out, and_4_out, and_5_out);
  and and_15 (and_15_out, and_7_out, and_8_out);
  and and_16 (and_16_out, and_10_out, and_11_out);
  and and_17 (Op1, and_13_out, and_3_out);
  and and_18 (MemRead, and_14_out, and_6_out);
  and and_19 (MemWrite, and_15_out, and_9_out);
  and and_20 (Branch, and_16_out, and_12_out);
  or or_1 (ALUSrc, MemWrite, MemRead);
  or or_2 (RegWrite, Op1, MemRead);

  assign MemToReg = MemRead;
  assign Op0 = Branch;
  assign RegDst = Op1;
endmodule

module ALUControl (
  input  Op0,
  input  Op1,
  input  [5:0] Funct,
  input  Zero,
  output [3:0] Operation
);

  wire and_1_out, and_2_out, and_3_out, and_4_out, and_5_out, and_6_out, and_7_out, and_8_out, and_9_out,
       and_10_out, and_11_out, and_12_out, and_13_out, and_14_out, and_15_out, and_16_out, and_17_out,
       and_18_out, and_19_out, and_20_out, and_21_out, and_22_out, and_23_out, and_24_out, and_25_out,
       and_26_out, and_27_out, and_28_out, and_29_out, and_30_out, and_32_out, and_33_out, and_34_out,
       not_1_out, not_2_out, not_3_out, not_4_out, not_5_out, not_6_out, not_7_out, not_8_out, not_9_out,
       not_10_out, not_11_out, not_12_out, not_13_out, not_14_out, not_15_out, not_16_out, not_17_out,
       not_18_out, not_19_out, not_20_out, not_21_out, not_22_out, not_23_out;

  not not_1 (not_1_out, Op0);
  not not_2 (not_2_out, Op1);
  not not_3 (not_3_out, Op1);
  not not_4 (not_4_out, Op0);
  not not_5 (not_5_out, Funct[0]);
  not not_6 (not_6_out, Funct[1]);
  not not_7 (not_7_out, Funct[2]);
  not not_8 (not_8_out, Funct[3]);
  not not_9 (not_9_out, Funct[4]);
  not not_10 (not_10_out, Funct[0]);
  not not_11 (not_11_out, Funct[2]);
  not not_12 (not_12_out, Funct[3]);
  not not_13 (not_13_out, Funct[4]);
  not not_14 (not_14_out, Funct[0]);
  not not_15 (not_15_out, Funct[1]);
  not not_16 (not_16_out, Funct[3]);
  not not_17 (not_17_out, Funct[4]);
  not not_18 (not_18_out, Funct[1]);
  not not_19 (not_19_out, Funct[3]);
  not not_20 (not_20_out, Funct[4]);
  not not_21 (not_21_out, Funct[0]);
  not not_22 (not_22_out, Funct[2]);
  not not_23 (not_23_out, Funct[4]);
  and and_1 (and_1_out, not_1_out, not_2_out);
  and and_2 (and_2_out, Op0, not_3_out);
  and and_3 (and_3_out, not_4_out, Op1);
  and and_4 (and_4_out, not_5_out, not_6_out);
  and and_5 (and_5_out, not_7_out, not_8_out);
  and and_6 (and_6_out, not_9_out, Funct[5]);
  and and_7 (and_7_out, not_10_out, Funct[1]);
  and and_8 (and_8_out, not_11_out, not_12_out);
  and and_9 (and_9_out, not_13_out, Funct[5]);
  and and_10 (and_10_out, not_14_out, not_15_out);
  and and_11 (and_11_out, Funct[2], not_16_out);
  and and_12 (and_12_out, not_17_out, Funct[5]);
  and and_13 (and_13_out, Funct[0], not_18_out);
  and and_14 (and_14_out, Funct[2], not_19_out);
  and and_15 (and_15_out, not_20_out, Funct[5]);
  and and_16 (and_16_out, not_21_out, Funct[1]);
  and and_17 (and_17_out, not_22_out, Funct[3]);
  and and_18 (and_18_out, not_23_out, Funct[5]);
  and and_19 (and_19_out, and_5_out, and_6_out);
  and and_20 (and_20_out, and_8_out, and_9_out);
  and and_21 (and_21_out, and_11_out, and_12_out);
  and and_22 (and_22_out, and_14_out, and_15_out);
  and and_23 (and_23_out, and_17_out, and_18_out);
  and and_24 (and_24_out, and_4_out, and_19_out);
  and and_25 (and_25_out, and_7_out, and_20_out);
  and and_26 (and_26_out, and_10_out, and_21_out);
  and and_27 (and_27_out, and_13_out, and_22_out);
  and and_28 (and_28_out, and_16_out, and_23_out);
  and and_29 (and_29_out, and_3_out, and_24_out);
  and and_30 (and_30_out, and_3_out, and_25_out);
  and and_31 (Operation[3], Zero, and_32_out);
  and and_32 (and_32_out, and_3_out, and_26_out);
  and and_33 (and_33_out, and_3_out, and_27_out);
  and and_34 (and_34_out, and_3_out, and_28_out);
  or or_1 (Operation[0], and_34_out, and_33_out, Operation[3]);
  or or_2 (Operation[1], and_34_out, and_1_out, and_29_out, and_30_out, and_2_out, Operation[3]);
  or or_3 (Operation[2], and_30_out, Operation[3], and_34_out, and_2_out);
endmodule

module Register32 (
  input  Clock,
  input  [31:0] DataIn,
  output [31:0] DataOut
);

  DLatch dlatch_1 (.C(Clock), .D(DataIn[0]), .Q(DataOut[0]));
  DLatch dlatch_2 (.C(Clock), .D(DataIn[1]), .Q(DataOut[1]));
  DLatch dlatch_3 (.C(Clock), .D(DataIn[2]), .Q(DataOut[2]));
  DLatch dlatch_4 (.C(Clock), .D(DataIn[3]), .Q(DataOut[3]));
  DLatch dlatch_5 (.C(Clock), .D(DataIn[4]), .Q(DataOut[4]));
  DLatch dlatch_6 (.C(Clock), .D(DataIn[5]), .Q(DataOut[5]));
  DLatch dlatch_7 (.C(Clock), .D(DataIn[6]), .Q(DataOut[6]));
  DLatch dlatch_8 (.C(Clock), .D(DataIn[7]), .Q(DataOut[7]));
  DLatch dlatch_9 (.C(Clock), .D(DataIn[8]), .Q(DataOut[8]));
  DLatch dlatch_10 (.C(Clock), .D(DataIn[9]), .Q(DataOut[9]));
  DLatch dlatch_11 (.C(Clock), .D(DataIn[10]), .Q(DataOut[10]));
  DLatch dlatch_12 (.C(Clock), .D(DataIn[11]), .Q(DataOut[11]));
  DLatch dlatch_13 (.C(Clock), .D(DataIn[12]), .Q(DataOut[12]));
  DLatch dlatch_14 (.C(Clock), .D(DataIn[13]), .Q(DataOut[13]));
  DLatch dlatch_15 (.C(Clock), .D(DataIn[14]), .Q(DataOut[14]));
  DLatch dlatch_16 (.C(Clock), .D(DataIn[15]), .Q(DataOut[15]));
  DLatch dlatch_17 (.C(Clock), .D(DataIn[16]), .Q(DataOut[16]));
  DLatch dlatch_18 (.C(Clock), .D(DataIn[17]), .Q(DataOut[17]));
  DLatch dlatch_19 (.C(Clock), .D(DataIn[18]), .Q(DataOut[18]));
  DLatch dlatch_20 (.C(Clock), .D(DataIn[19]), .Q(DataOut[19]));
  DLatch dlatch_21 (.C(Clock), .D(DataIn[20]), .Q(DataOut[20]));
  DLatch dlatch_22 (.C(Clock), .D(DataIn[21]), .Q(DataOut[21]));
  DLatch dlatch_23 (.C(Clock), .D(DataIn[22]), .Q(DataOut[22]));
  DLatch dlatch_24 (.C(Clock), .D(DataIn[23]), .Q(DataOut[23]));
  DLatch dlatch_25 (.C(Clock), .D(DataIn[24]), .Q(DataOut[24]));
  DLatch dlatch_26 (.C(Clock), .D(DataIn[25]), .Q(DataOut[25]));
  DLatch dlatch_27 (.C(Clock), .D(DataIn[26]), .Q(DataOut[26]));
  DLatch dlatch_28 (.C(Clock), .D(DataIn[27]), .Q(DataOut[27]));
  DLatch dlatch_29 (.C(Clock), .D(DataIn[28]), .Q(DataOut[28]));
  DLatch dlatch_30 (.C(Clock), .D(DataIn[29]), .Q(DataOut[29]));
  DLatch dlatch_31 (.C(Clock), .D(DataIn[30]), .Q(DataOut[30]));
  DLatch dlatch_32 (.C(Clock), .D(DataIn[31]), .Q(DataOut[31]));
endmodule
